# Fritzing sketch FubarinoSDController (saved by Fritzing 0.7.4b)

parts:
  FubarinoSD = IC, DIP package, 56 pins [chip_label=FubarinoSD spacing=900mil]
  P1 = Rotary Potentiometer (Large) [maximum_resistance=10kΩ package=THT]
  P2 = Rotary Potentiometer (Large) [maximum_resistance=10kΩ package=THT]
  Part1 = Triple Axis Accelerometer Breakout - ADXL335
  R1 = Resistor [tolerance=±5% resistance=10k package=THT]
  S1 = Pushbutton [package="[THT]"]

nets (from the pcb view):
  N1: FubarinoSD.pin2, R1.Pin_0
  N2: FubarinoSD.pin13, R1.Pin_1, S1.Pin_3, S1.Pin_4
  N3: FubarinoSD.pin28, S1.Pin_1, S1.Pin_2
  N4: FubarinoSD.pin29, P2.leg1
  N5: FubarinoSD.pin45, P2.wiper
  N6: FubarinoSD.pin48, Part1.ZOUT
  N7: FubarinoSD.pin49, Part1.YOUT
  N8: FubarinoSD.pin50, Part1.XOUT
  N9: FubarinoSD.pin51, P1.wiper
  N10: FubarinoSD.pin54, P1.leg2, P2.leg2, Part1.VCC
  N11: P1.leg1, Part1.GND
