# Fritzing sketch FubarinoAdapterShield (saved by Fritzing 0.7.4b)

parts:
  J3 = female pin header, 10 pins [form="♀ (female)"]  # not connected
  J4 = female pin header, 8 pins [form="♀ (female)"]  # not connected
  J5 = female pin header, 8 pins [form="♀ (female)"]  # not connected
  J6 = female pin header, 8 pins [form="♀ (female)"]  # not connected
  J7 = female pin header, 34 pins [form="♀ (female)"]  # not connected
  Power_plug1 = Power plug
  U1 = Voltage Regulator - 3.3V [package="TO220 [THT]"]
  J1 = female pin header, 28 pins [form="♀ (female)"]  # not connected
  J2 = female pin header, 28 pins [form="♀ (female)"]  # not connected
  J11 = female pin header, 10 pins [form="♀ (female)"]  # not connected
  J12 = female pin header, 8 pins [form="♀ (female)"]  # not connected
  J13 = female pin header, 8 pins [form="♀ (female)"]  # not connected

nets:
  N1: Power_plug1.VCC, U1.input_voltage
  GND: Power_plug1.GND, U1.GND

notes:
  AREF
