# Fritzing sketch FubarinoSDController (saved by Fritzing 0.7.4b)

parts:
  FubarinoSD = IC, DIP package, 56 pins [chip_label=FubarinoSD spacing=900mil]
  P1 = Rotary Potentiometer (Large) [maximum_resistance=10kΩ package=THT]
  P2 = Rotary Potentiometer (Large) [maximum_resistance=10kΩ package=THT]
  R1 = Resistor [tolerance=±5% resistance=10k package=THT]
  S1 = Pushbutton [package="[THT]"]
  J1 = female pin header, 7 pins [form="♀ (female)"]  # not connected

nets:
  N1: FubarinoSD.pin1, R1.Pin_0
  N2: FubarinoSD.pin2, S1.Pin_1, S1.Pin_2
  N3: FubarinoSD.pin13, R1.Pin_1, S1.Pin_3, S1.Pin_4
  N4: FubarinoSD.pin29, P2.leg1
  N5: FubarinoSD.pin45, P2.wiper
  N6: FubarinoSD.pin51, P1.wiper
  N7: FubarinoSD.pin54, P1.leg2, P2.leg2
  N8: FubarinoSD.pin56, P1.leg1
